# Fritzing sketch traffic_2 (saved by Fritzing 0.9.2b)
breadboards: 1

parts:
  Q1 = NPN-Transistor [package="TO92 [THT]"]
  R1 = Resistor [tolerance=±5% resistance=1k package=THT]
  LED1 = LED - 5mm [color="Green (560nm)" package="5 mm [THT]"]
  Q2 = NPN-Transistor [package="TO92 [THT]"]
  LED2 = LED - 5mm [color="Yellow (592nm)" package="5 mm [THT]"]
  R2 = Resistor [tolerance=±5% resistance=1k package=THT]
  Q3 = NPN-Transistor [package="TO92 [THT]"]
  R3 = Resistor [tolerance=±5% resistance=1k package=THT]
  LED3 = LED - 5mm [color="Red (633nm)" package="5 mm [THT]"]
  R4 = Resistor [tolerance=±5% resistance=330 package=THT]

nets:
  N1: Q1.E, Q2.E
  N2: Q1.B, R1.Pin_0
  N3: Q1.C, LED1.cathode
  N4: LED1.anode, LED2.anode, LED3.anode, R4.Pin_0
  N5: Q2.B, R2.Pin_0
  N6: Q2.C, LED2.cathode
  N7: Q3.B, R3.Pin_0
  N8: Q3.C, LED3.cathode

notes:
  pin0
  pin1
  pin2
  ground
  3 volts
